// Logisim project tp2_exo3.circ as structural Verilog: 5 circuits, main circuit main
module main (
  input  in_1,
  input  in_2,
  input  in_3,
  input  in_4,
  input  in_5,
  input  in_6,
  input  in_7,
  input  in_8,
  output out_9,
  output out_10,
  output out_11,
  output out_12,
  output out_13
);

  add4bit add4bit_1 (
    .in_1(in_5), .in_2(in_6), .in_3(in_7), .in_4(in_8), .in_5(in_1), .in_6(in_2), .in_7(in_3), .in_8(in_4),
    .out_9(out_9), .out_10(out_10), .out_11(out_11), .out_12(out_12), .out_13(out_13));
endmodule

module add1 (
  input  bit1,
  input  bit2,
  output Result,
  output Rs
);

  xor xor_1 (Result, bit1, bit2);
  and and_1 (Rs, bit1, bit2);
endmodule

module add2 (
  input  bit1,
  input  bit2,
  input  Re,
  output Rs,
  output BR1
);

  wire and_1_out, and_2_out, and_3_out, and_4_out, and_5_out, and_6_out, and_7_out, and_8_out, not_1_out,
       not_2_out, not_3_out, not_4_out, not_5_out, not_6_out, not_7_out, not_8_out, not_9_out;

  not not_1 (not_1_out, Re);
  not not_2 (not_2_out, bit2);
  not not_3 (not_3_out, bit1);
  not not_4 (not_4_out, bit2);
  not not_5 (not_5_out, Re);
  not not_6 (not_6_out, bit1);
  not not_7 (not_7_out, Re);
  not not_8 (not_8_out, bit1);
  not not_9 (not_9_out, bit2);
  and and_1 (and_1_out, bit1, bit2, not_1_out);
  and and_2 (and_2_out, bit1, not_2_out, Re);
  and and_3 (and_3_out, not_3_out, bit2, Re);
  and and_4 (and_4_out, bit1, bit2, Re);
  and and_5 (and_5_out, bit1, not_4_out, not_5_out);
  and and_6 (and_6_out, not_6_out, bit2, not_7_out);
  and and_7 (and_7_out, not_8_out, not_9_out, Re);
  and and_8 (and_8_out, bit1, bit2, Re);
  or or_1 (Rs, and_1_out, and_2_out, and_3_out, and_4_out);
  or or_2 (BR1, and_5_out, and_6_out, and_7_out, and_8_out);
endmodule

module add3 (
  input  in_1,
  input  B,
  input  A,
  output out_4,
  output out_5
);

  wire add1_1_result, add1_1_rs, add1_2_rs;

  add1 add1_1 (.bit1(A), .bit2(B), .Result(add1_1_result), .Rs(add1_1_rs));
  add1 add1_2 (.bit1(add1_1_result), .bit2(in_1), .Result(out_4), .Rs(add1_2_rs));
  or or_1 (out_5, add1_1_rs, add1_2_rs);
endmodule

module add4bit (
  input  in_1,
  input  in_2,
  input  in_3,
  input  in_4,
  input  in_5,
  input  in_6,
  input  in_7,
  input  in_8,
  output out_9,
  output out_10,
  output out_11,
  output out_12,
  output out_13
);

  wire add3_2_out_5, add3_3_out_5, add3_4_out_5;

  add3 add3_1 (.in_1(add3_2_out_5), .B(in_1), .A(in_5), .out_4(out_10), .out_5(out_9));
  add3 add3_2 (.in_1(add3_3_out_5), .B(in_2), .A(in_6), .out_4(out_11), .out_5(add3_2_out_5));
  add3 add3_3 (.in_1(add3_4_out_5), .B(in_3), .A(in_7), .out_4(out_12), .out_5(add3_3_out_5));
  add3 add3_4 (.in_1(1'b0), .B(in_4), .A(in_8), .out_4(out_13), .out_5(add3_4_out_5));
endmodule
